# Fritzing sketch hardware (saved by Fritzing 0.9.10b)
circuit board: 8.47cm x 6cm
breadboards: 1

parts:
  GY-NEO6MV2 = SUP500F [package=sup500f]
  RPI_Zero = Raspberry Pi Zero
  SIM900_SIM800 = SIM800L [package=THT]
  GY-91_(MPU-6050) = MPU-6050 Board GY-521 [form="♀ (female)" package=THT]
  D1 = Diode [package=diode-1n4001]
  C1 = Electrolytic Capacitor [capacitance=1μF voltage=35V package="0405 [SMD, electrolytic]"]
  VCC1 = 4 x AAA Battery Mount
  Pad1 = Pad [width=2.3760604884580623 height=2.6545144293629344 connect=center]
  Pad2 = Pad [width=2.3760604884580623 height=2.6545144293629344 connect=center]

nets:
  N1: GY-NEO6MV2.RX-I, RPI_Zero.pin_31
  N2: GY-NEO6MV2.TX-O, RPI_Zero.pin_33
  GND: GY-NEO6MV2.GND, RPI_Zero.pin_6, RPI_Zero.pin_25, RPI_Zero.pin_30, RPI_Zero.pin_39, SIM900_SIM800.GND, GY-91_(MPU-6050).pin2, C1.-, VCC1.-, Pad2.pad
  N3: GY-NEO6MV2.VCC, RPI_Zero.pin_2, RPI_Zero.pin_4, GY-91_(MPU-6050).pin1, D1.A, VCC1.+, Pad1.pad
  N4: RPI_Zero.pin_3, GY-91_(MPU-6050).pin4
  N5: RPI_Zero.pin_5, GY-91_(MPU-6050).pin3
  N6: RPI_Zero.pin_8, SIM900_SIM800.SIM_RXD
  N7: RPI_Zero.pin_10, SIM900_SIM800.SIM_TXD
  N8: SIM900_SIM800.5V, D1.C, C1.+

notes:
  GND: Black
  VCC: Red
  RX: white
  TX: Gray

custom parts:
  MPU-6050 Board GY-521: Acelerometro y Giroscopio MPU-6050 Board GY-521
